# Fritzing sketch button_test_sch (saved by Fritzing 0.9.3b)
breadboards: 1

parts:
  Raspberry_Pi_1 = Raspberry Pi 3 [part_number=RPI-3-V1.2]
  S1 = Round Pushbutton
  R3 = Resistor [tolerance=±5% resistance=1k package="2010 [SMD]"]

nets:
  N1: Raspberry_Pi_1.GND, S1.leg1
  N2: Raspberry_Pi_1.GIPO14, S1.leg0, R3.Pin_1
  N3: Raspberry_Pi_1.5V, R3.Pin_0

notes:
  --Cableado
  Negro=GND(Tierra) => Pin 14 RPi
  Rojo=+5V => Pin 4 RPi
  Verde=entrada digital datos => Pin 8 RPi
  --Componentes
  Botón 2 terminales
  Resistencia 1KΩ
  RPi2/3
  Circuito de prueba para el botón
