# Fritzing sketch sensor_test_sch (saved by Fritzing 0.9.3b)
breadboards: 1

parts:
  Raspberry_Pi_1 = Raspberry Pi 3 [part_number=RPI-3-V1.2]
  DS1 = DS18B20 1-Wire Temperature Sensor [part_number=DS18B20]
  R2 = Resistor [tolerance=±5% resistance=4.7k package="2010 [SMD]"]

nets:
  3V3: Raspberry_Pi_1.3v3, DS1.VDD, R2.Pin_0
  N1: Raspberry_Pi_1.GIPO4, DS1.DQ, R2.Pin_1
  GND: Raspberry_Pi_1.GND, DS1.GND

notes:
  Cableado
  Negro = GND (Tierra) => Pin39 RPi
  Rojo = +5V => Pin2 RPi
  Naranja = +3.3V => Pin1 RPi
  Azul = datos sensor => Pin7 RPi
  Componentes:
  Sensor DS18B20
  Resistencia 4.7KΩ
  RPi3/2
  Circuito de prueba para el sensor de temperatura
  DS18B20
