# Fritzing sketch thermometer_sch_2 (saved by Fritzing 0.9.3b)
breadboards: 1

parts:
  Raspberry_Pi_1 = Raspberry Pi 3 [part_number=RPI-3-V1.2]
  DS1 = DS18B20 1-Wire Temperature Sensor [part_number=DS18B20]
  R2 = Resistor [tolerance=±5% resistance=4.7k package="2010 [SMD]"]
  U1 = LCD-16X2 [package=lcd-16x2]
  U2 = POT [package=pot_alpha_rv16af-20]
  R3 = Resistor [tolerance=±5% resistance=1.5k package="2010 [SMD]"]
  S1 = Round Pushbutton
  R4 = Resistor [tolerance=±5% resistance=1k package="2010 [SMD]"]

nets:
  3V3: Raspberry_Pi_1.3v3, DS1.VDD, R2.Pin_1
  N1: Raspberry_Pi_1.GIPO4, DS1.DQ, R2.Pin_0
  GND: Raspberry_Pi_1.GND, DS1.GND, U1.VSS, U1.R_W, U1.K, U2.E, S1.leg1
  N2: Raspberry_Pi_1.GIPO7, U1.RS
  N3: Raspberry_Pi_1.GIPO8, U1.E
  N4: Raspberry_Pi_1.GIPO25, U1.DB4
  N5: Raspberry_Pi_1.GIPO24, U1.DB5
  N6: Raspberry_Pi_1.GIPO23, U1.DB6
  N7: Raspberry_Pi_1.GIPO18, U1.DB7
  N8: Raspberry_Pi_1.GIPO14, S1.leg0, R4.Pin_1
  5V: Raspberry_Pi_1.5V, U1.VDD, U2.A, R3.Pin_1, R4.Pin_0
  N9: U1.VO, U2.S
  N10: U1.A, R3.Pin_0

notes:
  Conexiones LCD
  <Pin LCD> => <Conexión>
  Pin1 => GND (Negro)
  Pin2 => +5V (rojo)
  Pin3 => Potenciómetro (Naranja)
  Pin4 => Pin26 RPi (Gris)
  Pin5 => GND (Negro)
  Pin6 => Pin24 RPi (Verde)
  Pin11 => Pin22 RPi (Amarillo)
  Pin12 => Pin18 RPi (Blanco)
  Pin13 => Pin16 RPi (Café)
  Pin14 => Pin12 RPi (Naranja)
  Pin15 => 5V con R1.5KΩ
  Pin16 => GND (Negro)
  Termómetro
  Componentes
  -RPi 2/3
  -LCD 2x16 líneas
  -Sensor DS18B20
  -Botón 2 terminales
  -Potenciómetro 5KΩ
  -Resistor 4.7KΩ
  -Resistor 1.5KΩ
  -Resistor 1KΩ
  Cables
  -Negro
  -Rojo
  -Azul
  -Amarillo
  -Naranja
  -Verde
  -Gris
  -Café
  -Blanco
  Pin1
  Pin16
  Potenciómetro
  5KΩ
